# Fritzing sketch circuit (saved by Fritzing 0.9.2b)
breadboards: 1

parts:
  부품1 = Arduino Uno (Rev3)
  부품2 = Arduino Uno (Rev3)
  R1 = PHOTOCELL [package=photocell-kit]
  R2 = PHOTOCELL [package=photocell-kit]
  R3 = PHOTOCELL [package=photocell-kit]
  R4 = PHOTOCELL [package=photocell-kit]
  R5 = PHOTOCELL [package=photocell-kit]
  R6 = PHOTOCELL [package=photocell-kit]
  R7 = PHOTOCELL [package=photocell-kit]
  R8 = PHOTOCELL [package=photocell-kit]
  R9 = PHOTOCELL [package=photocell-kit]
  R10 = PHOTOCELL [package=photocell-kit]
  R11 = Resistor [tolerance=±5% resistance=1k package="2010 [SMD]"]
  R12 = Resistor [tolerance=±5% resistance=1k package="2010 [SMD]"]
  R13 = Resistor [tolerance=±5% resistance=1k package="2010 [SMD]"]
  R14 = Resistor [tolerance=±5% resistance=1k package="2010 [SMD]"]
  R15 = Resistor [tolerance=±5% resistance=1k package="2010 [SMD]"]
  R16 = Resistor [tolerance=±5% resistance=1k package="2010 [SMD]"]
  R17 = Resistor [tolerance=±5% resistance=1k package="2010 [SMD]"]
  R18 = Resistor [tolerance=±5% resistance=1k package="2010 [SMD]"]
  R19 = Resistor [tolerance=±5% resistance=1k package="2010 [SMD]"]
  R20 = Resistor [tolerance=±5% resistance=1k package="2010 [SMD]"]
  LD1 = LD
  LD2 = LD
  LD3 = LD
  LD4 = LD
  LD5 = LD
  LD6 = LD
  LD7 = LD
  LD8 = LD
  LD9 = LD
  LD10 = LD
  부품3 = Arduino Nano (Rev3.0)

nets:
  N1: 부품1.A0, R1.P$1, R11.Pin_0
  N2: 부품1.A1, R2.P$1, R12.Pin_0
  N3: 부품1.A2, R3.P$1, R13.Pin_0
  N4: 부품1.A3, R4.P$1, R14.Pin_0
  N5: 부품1.A4/SDA, R5.P$1, R15.Pin_0
  N6: 부품1.5V, R11.Pin_1, R12.Pin_1, R13.Pin_1, R14.Pin_1, R15.Pin_1, R16.Pin_1, R17.Pin_1, R18.Pin_1, R19.Pin_1, R20.Pin_1
  GND: 부품1.GND, 부품2.GND
  N7: 부품2.A0, R6.P$1, R16.Pin_0
  N8: 부품2.A1, R7.P$1, R17.Pin_0
  N9: 부품2.A2, R8.P$1, R18.Pin_0
  N10: 부품2.A3, R9.P$1, R19.Pin_0
  N11: 부품2.A4/SDA, R10.P$1, R20.Pin_0
  N12: LD1.cathode, LD2.cathode, LD3.cathode, LD4.cathode, LD5.cathode, LD6.cathode, LD7.cathode, LD8.cathode, LD9.cathode, LD10.cathode, 부품3.GND
  N13: LD1.anode, 부품3.D13/SCK
  N14: LD2.anode, 부품3.D12/MISO
  N15: LD3.anode, 부품3.D11/MOSI
  N16: LD4.anode, 부품3.D10
  N17: LD5.anode, 부품3.D9
  N18: LD6.anode, 부품3.D8
  N19: LD7.anode, 부품3.D7
  N20: LD8.anode, 부품3.D6
  N21: LD9.anode, 부품3.D5
  N22: LD10.anode, 부품3.D4

custom parts:
  LD: A Generic Red Dot Laser Diode Module (~5mW)
